// Logisim project ALU.circ as structural Verilog: 1 circuit, main circuit main
module main (
  input  [7:0] in_1,
  input  [7:0] in_2,
  input  [2:0] in_3,
  output [7:0] RESULT
);

  wire [7:0] adder_1_out, and_1_out, divider_1_out, multiplier_1_out, not_1_out, or_1_out, subtractor_1_out,
       xor_1_out;

  Adder adder_1 (.a(in_1), .b(in_2), .out(adder_1_out));  // open: cin, cout
  Subtractor subtractor_1 (.a(in_1), .b(in_2), .out(subtractor_1_out));  // open: bin, bout
  Multiplier multiplier_1 (.a(in_1), .b(in_2), .out(multiplier_1_out));  // open: cin, cout
  Divider divider_1 (.a(in_1), .b(in_2), .out(divider_1_out));  // open: upper, rem
  assign and_1_out = in_1 & in_2;  // AND_Gate and_1, 8 bits wide
  assign or_1_out = in_1 | in_2;  // OR_Gate or_1, 8 bits wide
  assign xor_1_out = in_1 ^ in_2;  // XOR_Gate xor_1, 8 bits wide
  assign not_1_out = ~in_1;  // NOT_Gate not_1, 8 bits wide
  Multiplexer #(.select(3), .width(8)) multiplexer_1 (
    .in0(adder_1_out), .in1(subtractor_1_out), .in2(multiplier_1_out), .in3(divider_1_out), .in4(and_1_out),
    .in5(or_1_out), .in6(xor_1_out), .in7(not_1_out), .out(RESULT), .sel(in_3));

  // Notes on the sheet:
  //   A
  //   B
  //   ADD
  //   SUB
  //   MULT
  //   DIV
  //   OR
  //   NOT A
  //   8 bit ALU
  //   AND
  //   XOR
  //   OP
  //   OP = 000 → ADD
  //   OP = 001 → SUB
  //   OP = 010 → MUL
  //   OP = 011 → DIV
  //   OP = 100 → AND
  //   OP = 101 → OR
  //   OP = 110 → XOR
  //   OP = 111 → NOT A
endmodule
