// Logisim project Adder_Mux_8_1.circ as structural Verilog: 1 circuit, main circuit main
module main (
  input  in_1,
  input  in_2,
  input  in_3,
  input  in_4,
  input  [2:0] in_5,
  output out_6,
  output out_7
);

  Multiplexer #(.select(3)) multiplexer_1 (
    .in0(in_1), .in1(in_2), .in2(in_2), .in3(in_1), .in4(in_2), .in5(in_1), .in6(in_1), .in7(in_2),
    .out(out_6), .sel(in_5));
  Multiplexer #(.select(3)) multiplexer_2 (
    .in0(in_3), .in1(in_3), .in2(in_3), .in3(in_4), .in4(in_3), .in5(in_4), .in6(in_4), .in7(in_4),
    .out(out_7), .sel(in_5));
endmodule
