// Logisim project HalfAdder.circ as structural Verilog: 1 circuit, main circuit main
module main (
  input  A,
  input  B,
  output S,
  output C
);

  xor xor_1 (S, A, B);
  and and_1 (C, B, A);

  // Notes on the sheet:
  //   HALF ADDER
  //   A | B | S | C |
  //   ---------------
  //   0 | 0 | 0 | 0 |
  //   ---------------
  //   0 | 1 | 1 | 0 |
  //   ---------------
  //   1 | 0 | 1 | 0 |
  //   ---------------
  //   1 | 1 | 0 | 1 |
  //   S=A'B + AB'  => A XOR B
  //   C=A.B
endmodule
