// Logisim project HalfSubtractor.circ as structural Verilog: 1 circuit, main circuit main
module main (
  input  A,
  input  Bi,
  output S,
  output Bo
);

  wire not_1_out;

  not not_1 (not_1_out, A);
  xor xor_1 (S, A, Bi);
  and and_1 (Bo, Bi, not_1_out);

  // Notes on the sheet:
  //   HALF Subtractor
  //   A | B | D | B |
  //   ---------------
  //   0 | 0 | 0 | 0 |
  //   ---------------
  //   0 | 1 | 1 | 1 |
  //   ---------------
  //   1 | 0 | 1 | 0 |
  //   ---------------
  //   1 | 1 | 0 | 0 |
endmodule
