// Logisim project RippleAdder.circ as structural Verilog: 1 circuit, main circuit main
module main (
  input  in_1,
  input  in_2,
  input  in_3,
  input  in_4,
  input  in_5,
  input  in_6,
  input  in_7,
  input  in_8,
  input  in_9,
  output out_10,
  output out_11,
  output out_12,
  output out_13,
  output out_14,
  output out_15,
  output out_16,
  output out_17
);

  wire and_1_out, and_2_out, and_3_out, and_4_out, and_5_out, and_6_out, and_7_out, and_8_out, and_9_out,
       and_10_out, and_11_out, and_12_out, and_13_out, and_14_out, and_15_out, and_16_out, and_17_out,
       and_18_out, and_19_out, and_20_out, and_21_out, and_22_out, and_23_out, and_24_out, and_25_out,
       and_26_out, and_27_out, and_28_out, not_1_out, not_2_out, not_3_out, not_4_out, not_5_out, not_6_out,
       not_7_out, not_8_out, not_9_out, not_10_out, not_11_out, not_12_out;

  not not_1 (not_1_out, in_7);
  not not_2 (not_2_out, in_8);
  not not_3 (not_3_out, in_9);
  and and_1 (and_1_out, not_1_out, not_2_out, in_9);
  and and_2 (and_2_out, not_1_out, in_8, not_3_out);
  and and_3 (and_3_out, in_7, not_2_out, not_3_out);
  and and_4 (and_4_out, in_7, in_8, in_9);
  and and_5 (and_5_out, in_7, in_8);
  and and_6 (and_6_out, in_8, in_9);
  and and_7 (and_7_out, in_7, in_9);
  or or_1 (out_13, and_1_out, and_2_out, and_3_out, and_4_out);
  or or_2 (out_17, and_5_out, and_6_out, and_7_out);
  not not_4 (not_4_out, in_5);
  not not_5 (not_5_out, in_6);
  not not_6 (not_6_out, out_17);
  and and_8 (and_8_out, not_4_out, not_5_out, out_17);
  and and_9 (and_9_out, not_4_out, in_6, not_6_out);
  and and_10 (and_10_out, in_5, not_5_out, not_6_out);
  and and_11 (and_11_out, in_5, in_6, out_17);
  and and_12 (and_12_out, in_5, in_6);
  and and_13 (and_13_out, in_6, out_17);
  and and_14 (and_14_out, in_5, out_17);
  or or_3 (out_12, and_8_out, and_9_out, and_10_out, and_11_out);
  or or_4 (out_16, and_12_out, and_13_out, and_14_out);
  not not_7 (not_7_out, in_3);
  not not_8 (not_8_out, in_4);
  not not_9 (not_9_out, out_16);
  and and_15 (and_15_out, not_7_out, not_8_out, out_16);
  and and_16 (and_16_out, not_7_out, in_4, not_9_out);
  and and_17 (and_17_out, in_3, not_8_out, not_9_out);
  and and_18 (and_18_out, in_3, in_4, out_16);
  and and_19 (and_19_out, in_3, in_4);
  and and_20 (and_20_out, in_4, out_16);
  and and_21 (and_21_out, in_3, out_16);
  or or_5 (out_11, and_15_out, and_16_out, and_17_out, and_18_out);
  or or_6 (out_15, and_19_out, and_20_out, and_21_out);
  not not_10 (not_10_out, in_1);
  not not_11 (not_11_out, in_2);
  not not_12 (not_12_out, out_15);
  and and_22 (and_22_out, not_10_out, not_11_out, out_15);
  and and_23 (and_23_out, not_10_out, in_2, not_12_out);
  and and_24 (and_24_out, in_1, not_11_out, not_12_out);
  and and_25 (and_25_out, in_1, in_2, out_15);
  and and_26 (and_26_out, in_1, in_2);
  and and_27 (and_27_out, in_2, out_15);
  and and_28 (and_28_out, in_1, out_15);
  or or_7 (out_10, and_22_out, and_23_out, and_24_out, and_25_out);
  or or_8 (out_14, and_26_out, and_27_out, and_28_out);
endmodule
