// Logisim project RippleAdder_2.circ as structural Verilog: 1 circuit, main circuit main
module main (
  input  [3:0] A,
  input  [3:0] in_2,
  input  [3:0] in_3,
  output out_4,
  output [3:0] out_5,
  output [3:0] out_6,
  output [3:0] out_7,
  output [3:0] out_8
);

  wire adder_1_cout, adder_2_cout, adder_3_cout;

  Adder #(.width(4)) adder_1 (.a(in_2), .b(A), .out(out_7), .cout(adder_1_cout));  // open: cin
  Adder #(.width(4)) adder_2 (.a(in_2), .b(A), .out(out_8), .cin(adder_1_cout), .cout(adder_2_cout));
  Adder #(.width(4)) adder_3 (.a(in_2), .b(A), .out(out_6), .cin(adder_2_cout), .cout(adder_3_cout));
  Adder #(.width(4)) adder_4 (.a(in_2), .b(A), .out(out_5), .cin(adder_3_cout), .cout(out_4));

  // Notes on the sheet:
  //   B
  //   Cin
endmodule
