// Logisim project De_coder.circ as structural Verilog: 1 circuit, main circuit main
module main (
  input  in_1,
  input  in_2,
  input  in_3,
  output out_4,
  output out_5,
  output out_6,
  output out_7,
  output out_8,
  output out_9,
  output out_10,
  output out_11
);

  wire not_1_out, not_2_out, not_3_out;

  not not_1 (not_1_out, in_1);
  not not_2 (not_2_out, in_2);
  not not_3 (not_3_out, in_3);
  and and_1 (out_4, not_3_out, not_2_out, not_1_out);
  and and_2 (out_5, in_3, not_2_out, not_1_out);
  and and_3 (out_6, not_3_out, in_2, not_1_out);
  and and_4 (out_7, in_3, in_2, not_1_out);
  and and_5 (out_8, not_3_out, not_2_out, in_1);
  and and_6 (out_9, in_3, not_2_out, in_1);
  and and_7 (out_10, not_3_out, in_2, in_1);
  and and_8 (out_11, in_3, in_2, in_1);

  // Notes on the sheet:
  //   A2
  //   A1
  //   A0
endmodule
