// Logisim project Encoder.circ as structural Verilog: 1 circuit, main circuit main
module main (
  input  D9,
  input  in_2,
  input  in_3,
  input  in_4,
  input  in_5,
  input  in_6,
  input  in_7,
  input  in_8,
  input  D1,
  output out_10,
  output out_11,
  output out_12,
  output B0
);

  or or_1 (out_10, D9, in_2);
  or or_2 (out_11, in_3, in_4, in_5, in_6);
  or or_3 (out_12, in_3, in_4, in_7, in_8);
  or or_4 (B0, in_3, in_5, D9, in_7, D1);

  // Notes on the sheet:
  //   B3
endmodule
