// Logisim project MUX.circ as structural Verilog: 1 circuit, main circuit main
module main (
  input  in_1,
  input  in_2,
  input  I0,
  input  I1,
  input  I2,
  input  I3,
  input  G,
  output out_8
);

  wire nand_1_out, nand_2_out, nand_3_out, nand_4_out, not_1_out, not_2_out, not_3_out;

  not not_1 (not_1_out, in_1);
  not not_2 (not_2_out, G);
  not not_3 (not_3_out, in_2);
  nand nand_1 (nand_1_out, I0, not_3_out, not_1_out, not_2_out);
  nand nand_2 (nand_2_out, I1, in_2, not_1_out, not_2_out);
  nand nand_3 (nand_3_out, I2, not_3_out, in_1, not_2_out);
  nand nand_4 (nand_4_out, I3, in_2, in_1, not_2_out);
  nand nand_5 (out_8, nand_1_out, nand_2_out, nand_3_out, nand_4_out);

  // Notes on the sheet:
  //   S1
  //   S0
  //   Mux
endmodule
