// Logisim project BiDirectReg.circ as structural Verilog: 1 circuit, main circuit main
module main (
  input  in_1
);

  wire and_1_out, and_2_out, and_3_out, and_4_out, and_5_out, and_6_out, and_7_out, and_8_out, clock_1_out,
       or_1_out, or_2_out, or_3_out, or_4_out, undriven, undriven_2, undriven_3, undriven_4, undriven_5,
       undriven_6, undriven_7, undriven_8, undriven_9, undriven_10, undriven_11, undriven_12, undriven_13,
       undriven_14, undriven_15, undriven_16;

  Clock clock_1 (.out(clock_1_out));
  and and_1 (and_1_out, undriven, undriven_2);
  and and_2 (and_2_out, undriven_3, undriven_4);
  or or_1 (or_1_out, and_1_out, and_2_out);
  D_Flip_Flop d_ff_1 (.D(or_1_out), .clk(clock_1_out), .reset(in_1));  // open: Q, Qn, preset
  and and_3 (and_3_out, undriven_5, undriven_6);
  and and_4 (and_4_out, undriven_7, undriven_8);
  or or_2 (or_2_out, and_3_out, and_4_out);
  D_Flip_Flop d_ff_2 (.D(or_2_out), .clk(clock_1_out), .reset(in_1));  // open: Q, Qn, preset
  and and_5 (and_5_out, undriven_9, undriven_10);
  and and_6 (and_6_out, undriven_11, undriven_12);
  or or_3 (or_3_out, and_5_out, and_6_out);
  D_Flip_Flop d_ff_3 (.D(or_3_out), .clk(clock_1_out), .reset(in_1));  // open: Q, Qn, preset
  and and_7 (and_7_out, undriven_13, undriven_14);
  or or_4 (or_4_out, and_7_out, and_8_out);
  and and_8 (and_8_out, undriven_15, undriven_16);
  D_Flip_Flop d_ff_4 (.D(or_4_out), .clk(clock_1_out), .reset(in_1));  // open: Q, Qn, preset
endmodule
