// Logisim project ShiftReg.circ as structural Verilog: 1 circuit, main circuit main
module main (
  input  in_1,
  input  in_2,
  input  in_3,
  input  in_4,
  input  in_5,
  input  in_6,
  input  in_7,
  input  in_8,
  input  in_9,
  input  in_10,
  input  in_11,
  input  in_12,
  input  in_13,
  input  in_14,
  input  in_15,
  input  in_16,
  input  in_17,
  input  in_18,
  input  in_19,
  output out_20,
  output out_21,
  output out_22,
  output out_23,
  output out_24,
  output out_25,
  output out_26,
  output out_27,
  output out_28,
  output out_29
);

  wire clock_1_out, clock_2_out, clock_3_out, clock_4_out, d_ff_2_q, d_ff_3_q, d_ff_6_q, d_ff_7_q, d_ff_10_q,
       d_ff_14_q, multiplexer_1_out, multiplexer_2_out, multiplexer_3_out, multiplexer_4_out;

  Clock clock_1 (.out(clock_1_out));
  Clock clock_2 (.out(clock_2_out));
  Clock clock_3 (.out(clock_3_out));
  Multiplexer multiplexer_1 (.in0(in_5), .in1(in_13), .out(multiplexer_1_out), .sel(in_6));
  Clock clock_4 (.out(clock_4_out));
  D_Flip_Flop d_ff_1 (.D(in_1), .clk(clock_2_out), .Q(out_20), .reset(in_2));  // open: Qn, preset
  D_Flip_Flop d_ff_2 (.D(in_3), .clk(clock_3_out), .Q(d_ff_2_q), .reset(in_4));  // open: Qn, preset
  D_Flip_Flop d_ff_3 (.D(multiplexer_1_out), .clk(clock_1_out), .Q(d_ff_3_q), .reset(in_10));  // open: Qn, preset
  D_Flip_Flop d_ff_4 (.D(in_16), .clk(clock_4_out), .Q(out_26), .reset(in_15));  // open: Qn, preset
  D_Flip_Flop d_ff_5 (.D(out_20), .clk(clock_2_out), .Q(out_21), .reset(in_2));  // open: Qn, preset
  D_Flip_Flop d_ff_6 (.D(d_ff_2_q), .clk(clock_3_out), .Q(d_ff_6_q), .reset(in_4));  // open: Qn, preset
  Multiplexer multiplexer_2 (.in0(d_ff_3_q), .in1(in_14), .out(multiplexer_2_out), .sel(in_7));
  D_Flip_Flop d_ff_7 (.D(multiplexer_2_out), .clk(clock_1_out), .Q(d_ff_7_q), .reset(in_10));  // open: Qn, preset
  D_Flip_Flop d_ff_8 (.D(in_17), .clk(clock_4_out), .Q(out_27), .reset(in_15));  // open: Qn, preset
  D_Flip_Flop d_ff_9 (.D(out_21), .clk(clock_2_out), .Q(out_22), .reset(in_2));  // open: Qn, preset
  D_Flip_Flop d_ff_10 (.D(d_ff_6_q), .clk(clock_3_out), .Q(d_ff_10_q), .reset(in_4));  // open: Qn, preset
  D_Flip_Flop d_ff_11 (.D(in_18), .clk(clock_4_out), .Q(out_28), .reset(in_15));  // open: Qn, preset
  D_Flip_Flop d_ff_12 (.D(out_22), .clk(clock_2_out), .Q(out_23), .reset(in_2));  // open: Qn, preset
  D_Flip_Flop d_ff_13 (.D(d_ff_10_q), .clk(clock_3_out), .Q(out_24), .reset(in_4));  // open: Qn, preset
  D_Flip_Flop d_ff_14 (.D(multiplexer_3_out), .clk(clock_1_out), .Q(d_ff_14_q), .reset(in_10));  // open: Qn, preset
  Multiplexer multiplexer_3 (.in0(d_ff_7_q), .in1(in_11), .out(multiplexer_3_out), .sel(in_8));
  D_Flip_Flop d_ff_15 (.D(in_19), .clk(clock_4_out), .Q(out_29), .reset(in_15));  // open: Qn, preset
  Multiplexer multiplexer_4 (.in0(d_ff_14_q), .in1(in_12), .out(multiplexer_4_out), .sel(in_9));
  D_Flip_Flop d_ff_16 (.D(multiplexer_4_out), .clk(clock_1_out), .Q(out_25), .reset(in_10));  // open: Qn, preset

  // Notes on the sheet:
  //   1.SIPO
  //   2.SISO
  //   3.PISO
  //   4.PIPO
endmodule
